# Fritzing sketch Protoboard (saved by Fritzing 0.9.3b)
breadboards: 1

parts:
  BeagleBone1 = BeagleBone Black
  LED1 = LED - 5mm [color="Red (633nm)" package="5 mm [THT]"]
  LED2 = LED - 5mm [color="Green (555nm)" package="5 mm [THT]"]
  LED3 = LED - 5mm [color="Yellow (595nm)" package="5 mm [THT]"]
  R1 = Resistor [tolerance=±5% resistance=220 package=THT]
  R2 = Resistor [tolerance=±5% resistance=220 package=THT]
  R3 = Resistor [tolerance=±5% resistance=220 package=THT]
  S1 = Pushbutton [package="[THT]"]

nets:
  N1: BeagleBone1.no_name_yet#1, R1.Pin_0, R2.Pin_0, R3.Pin_0
  N2: BeagleBone1.no_name_yet#3, S1.Pin_3, S1.Pin_4
  N3: BeagleBone1.no_name_yet#14, LED1.cathode
  N4: BeagleBone1.no_name_yet#16, LED3.cathode
  N5: BeagleBone1.no_name_yet#22, LED2.cathode
  N6: BeagleBone1.no_name_yet#30, S1.Pin_1, S1.Pin_2
  N7: LED1.anode, R1.Pin_1
  N8: LED2.anode, R2.Pin_1
  N9: LED3.anode, R3.Pin_1

custom parts:
  BeagleBone Black: BeagleBone Black rev. A5B
