# Fritzing sketch Protoboard (saved by Fritzing 0.9.3b)
breadboards: 1

parts:
  R1 = Rotary Potentiometer (Small) [maximum_resistance=100kΩ package=THT]
  R2 = Photocell (LDR) [package=THT]
  S1 = Pushbutton [package="[THT]"]
  R3 = Resistor [tolerance=±5% resistance=220 package=THT]
  BeagleBone1 = BeagleBone Black

nets:
  N1: R1.leg1, R1.leg2, R2.pin_0, BeagleBone1.no_name_yet#30
  N2: R1.wiper, BeagleBone1.no_name_yet#40
  N3: R2.pin_1, R3.Pin_0, BeagleBone1.no_name_yet#33
  N4: S1.Pin_1, S1.Pin_2, BeagleBone1.no_name_yet#27
  N5: S1.Pin_3, S1.Pin_4, BeagleBone1.no_name_yet#3
  N6: R3.Pin_1, BeagleBone1.no_name_yet#34

custom parts:
  BeagleBone Black: BeagleBone Black rev. A5B
