# Fritzing sketch Client (saved by Fritzing 0.9.3b)
breadboards: 1

parts:
  BeagleBone1 = BeagleBone Black
  GPIO_115_(up) = Pushbutton [package="[SMD]"]
  GPIO_20(down) = Pushbutton [package="[SMD]"]
  GPIO_7_(play) = Pushbutton [package="[SMD]"]
  AIN_1 = Rotary Potentiometer (Small) [maximum_resistance=100kΩ package=THT]

nets:
  N1: BeagleBone1.no_name_yet#3, GPIO_115_(up).Pin_3, GPIO_115_(up).Pin_4, GPIO_20(down).Pin_3, GPIO_20(down).Pin_4, GPIO_7_(play).Pin_3, GPIO_7_(play).Pin_4
  N2: BeagleBone1.no_name_yet#27, GPIO_115_(up).Pin_1, GPIO_115_(up).Pin_2
  N3: BeagleBone1.no_name_yet#32, AIN_1.leg2
  N4: BeagleBone1.no_name_yet#34, AIN_1.leg1
  N5: BeagleBone1.no_name_yet#40, AIN_1.wiper
  N6: BeagleBone1.no_name_yet#41, GPIO_20(down).Pin_1, GPIO_20(down).Pin_2
  N7: BeagleBone1.no_name_yet#42, GPIO_7_(play).Pin_1, GPIO_7_(play).Pin_2

custom parts:
  BeagleBone Black: BeagleBone Black rev. A5B
